# Fritzing sketch IOT-Project1 (saved by Fritzing 0.9.4)
circuit board: 8.46667cm x 5.64444cm
breadboards: 1

parts:
  Part1 = Arduino Uno (Rev3)
  S1 = Momentary Switch [package=ksa_sealed_tac_switch]
  S2 = Momentary Switch [package=ksa_sealed_tac_switch]
  S3 = Momentary Switch [package=ksa_sealed_tac_switch]
  S4 = Momentary Switch [package=ksa_sealed_tac_switch]
  R1 = Rotary Potentiometer (Small) [maximum_resistance=10kΩ package=THT]
  LED1 = LED - 5mm [color="Green (570nm)" package="5 mm [THT]"]
  LED2 = LED - 5mm [color="Green (570nm)" package="5 mm [THT]"]
  LED3 = LED - 5mm [color="Green (570nm)" package="5 mm [THT]"]
  LED4 = LED - 5mm [color="Green (570nm)" package="5 mm [THT]"]
  LED5 = LED - 5mm [color="Red (633nm)" package="5 mm [THT]"]
  R2 = Resistor [tolerance=±5% resistance=10k package="0402 [SMD]"]
  R3 = Resistor [tolerance=±5% resistance=10k package="0402 [SMD]"]
  R4 = Resistor [tolerance=±5% resistance=10k package="0402 [SMD]"]
  R5 = Resistor [tolerance=±5% resistance=10k package="0402 [SMD]"]
  R6 = Resistor [tolerance=±5% resistance=10k package="0402 [SMD]"]
  R7 = Resistor [tolerance=±5% resistance=10k package="0402 [SMD]"]
  R8 = Resistor [tolerance=±5% resistance=10k package="0402 [SMD]"]
  R9 = Resistor [tolerance=±5% resistance=10k package="0402 [SMD]"]
  R10 = Resistor [tolerance=±5% resistance=10k package="0402 [SMD]"]

nets:
  N1: Part1.A0, R1.wiper
  N2: Part1.D10_PWM/SS, S1.2, R10.Pin_0
  N3: Part1.D11_PWM/MOSI, S2.2, R9.Pin_0
  N4: Part1.D12/MISO, S3.2, R8.Pin_0
  N5: Part1.D13/SCK, S4.2, R7.Pin_0
  N6: Part1.GND, R1.leg2, R2.Pin_1, R3.Pin_1, R4.Pin_1, R5.Pin_1, R6.Pin_1, R7.Pin_1, R8.Pin_1, R9.Pin_1, R10.Pin_1
  N7: Part1.D2, LED1.anode
  N8: Part1.D3_PWM, LED2.anode
  N9: Part1.D4, LED3.anode
  N10: Part1.D5_PWM, LED4.anode
  N11: Part1.D6_PWM, LED5.anode
  N12: Part1.5V, S1.4, S2.4, S3.4, S4.4, R1.leg1
  N13: LED1.cathode, R6.Pin_0
  N14: LED2.cathode, R5.Pin_0
  N15: LED3.cathode, R4.Pin_0
  N16: LED4.cathode, R3.Pin_0
  N17: LED5.cathode, R2.Pin_0
